// Digital circuit halfAdder.dig as structural Verilog
module halfAdder (
  input  i_A,
  input  i_B,
  output o_Cout,
  output o_S
);

  and and_1 (o_Cout, i_A, i_B);
  xor xor_1 (o_S, i_A, i_B);
endmodule

/* Test case Tests:
i_A i_B o_S o_Cout
0 0 0 0 
0 1 1 0
1 0 1 0
1 1 0 1
*/
